# Fritzing sketch esp32cam (saved by Fritzing 0.9.1b)

parts:
  ESP32_-_Back1 = ESP32 - CAM
  J2 = Basic Servo
  Part1 = Power Cell LiPo Charger/Booster
  J1 = Basic Servo
  U1 = LIPO-110mAh [package=lipo-110]

nets:
  GND: ESP32_-_Back1.GND, J2.gnd, Part1.GND, J1.gnd, U1.-
  VCC: ESP32_-_Back1.5V, J2.vcc, Part1.VCC, J1.vcc
  N1: ESP32_-_Back1.GPIO16, J2.pulse
  N2: ESP32_-_Back1.GPIO0, J1.pulse
  N3: Part1.VBATT, U1.+

notes:
  Battery Charger Module Boost
  GPIO12
  GPIO13
  PAN
  TILT
  SG90

custom parts:
  ESP32 - CAM: The ESP32-CAM has a very competitive small-size camera module that can operate independently as a minimum system with a footprint of only 27*40.5*4.5mm and a deep sleep current of up to 6mA.
